// Logisim project ex3.circ as structural Verilog: 1 circuit, main circuit AddMachine
module AddMachine (
  input  clk,
  output [7:0] ADD_OUT,
  output [7:0] REG_OUT
);

  wire [7:0] adder_1_out;

  Adder adder_1 (.a(REG_OUT), .b(8'h1), .out(adder_1_out));  // open: cin, cout
  Register register_1 (.D(adder_1_out), .clk(clk), .Q(REG_OUT));  // open: en, clr
endmodule
