// Logisim project ex4.circ as structural Verilog: 5 circuits, main circuit RotRight
module RotRight (
  input  [15:0] INPUT0,
  input  [3:0] AMOUNT,
  output [15:0] OUTPUT0
);

  rot1 rot1_1 ();  // open: in_1, out_2
  rot2 rot2_1 ();  // open: in_1, out_2
  rot4 rot4_1 ();  // open: in_1, out_2
  rot8 rot8_1 ();  // open: in_1, out_2
endmodule

module rot1 (
  input  [15:0] in_1,
  output [15:0] out_2
);
endmodule

module rot2 (
  input  [15:0] in_1,
  output [15:0] out_2
);
endmodule

module rot4 (
  input  [15:0] in_1,
  output [15:0] out_2
);
endmodule

module rot8 (
  input  [15:0] in_1,
  output [15:0] out_2
);
endmodule
